# Fritzing sketch PongDue (saved by Fritzing 0.9.2b)

parts:
  U1 = Wiichuck Adapter
  U2 = Wiichuck Adapter
  Part1 = Arduino Due (Rev2b)
  U3 = 10-pin Header for 16x24 HT1632C Red LED Matrix [part_number=555 package=HT1632C]

nets:
  N1: U1.-, U2.-, Part1.GND, U3.6
  N2: U1.+, U2.+, Part1.IOREF
  N3: U1.SDA, Part1.D20/SDA3
  N4: U1.SCL, Part1.D21/SCL3
  N5: U2.SDA, Part1.SDA1
  N6: U2.SCL, Part1.SCL1
  N7: Part1.5V, U3.2
  N8: Part1.D4_PWM/SS1, U3.8
  N9: Part1.D5_PWM, U3.7
  N10: Part1.D6_PWM, U3.4

custom parts:
  Wiichuck Adapter: SCP1000 Barometric Pressure sensor. Can sense air pressure and temperature. SPI interface.
  10-pin Header for 16x24 HT1632C Red LED Matrix: Adafruit 16x24 Red LED Matrix Panel HT1632C This is the upper left 10 pin connector near the J5 jumper. Part #555 at Adafruit
